# Fritzing sketch blink (saved by Fritzing 1.0.3b)

parts:
  J1 = male pin header, 2 pins [form="♂ (male)"]
  J2 = male pin header, 8 pins [form="♂ (male)"]  # not connected
  J3 = male pin header, 8 pins [form="♂ (male)"]  # not connected
  J4 = male pin header, 8 pins [form="♂ (male)"]  # not connected
  J5 = male pin header, 8 pins [form="♂ (male)"]

nets:
  N1: J1.pin1, J5.pin2
  N2: J1.pin2, J5.pin3
